// Digital circuit ALU.dig as structural Verilog
module ALU (
  input  [7:0] A,
  input  [7:0] B,
  input  [2:0] Select,
  input  CLK,
  output [7:0] S,
  output [7:0] MQ,
  output [7:0] AC,
  output [7:0] MQ_2
);

  wire [7:0] div_1_r, left_shift_1_p2, MQ0, MQ1, nand_8bit_1_s, right_shift_1_p2, S_t, soma_8bit_1_s,
       subtracao_8bit_1_s, xor_8bit_1_p5, xor_8bit_1_p6;

  Soma_8bit soma_8bit_1 (.A(A), .B(B), .Cin(1'b0), .S(soma_8bit_1_s));  // open: Cout
  Subtracao_8bit subtracao_8bit_1 (.A(A), .B(B), .Cin(1'b0), .S(subtracao_8bit_1_s));  // open: Cout
  NAND_8bit nand_8bit_1 (.A(A), .B(B), .S(nand_8bit_1_s));
  // XOR_8bit xor_8bit_1: pin names not known; wires that end beside it: A, B, A, B, {MQ0, xor_8bit_1_p5}, xor_8bit_1_p6
  // Left_Shift left_shift_1: pin names not known; wires that end beside it: A, left_shift_1_p2
  // Right_Shift right_shift_1: pin names not known; wires that end beside it: A, right_shift_1_p2
  Div #(.Bits(8)) div_1 (.a(A), .b(B), .q(MQ1), .r(div_1_r));
  Multiplexer #(.Selector_Bits(3), .Bits(8)) multiplexer_1 (
    .sel(Select), .in_0(soma_8bit_1_s), .in_1(subtracao_8bit_1_s), .in_2(xor_8bit_1_p5),
    .in_3(nand_8bit_1_s), .in_4(xor_8bit_1_p6), .in_5(left_shift_1_p2), .in_6(right_shift_1_p2),
    .in_7(div_1_r), .out(S));
  Register #(.Bits(8)) u_MQ (.D(MQ1), .C(CLK), .en(1'b1), .Q(MQ));
  Register #(.Bits(8)) u_MQ_2 (.D(MQ0), .C(CLK), .en(1'b1), .Q(MQ_2));
  Register #(.Bits(8)) u_AC (.D(S_t), .C(CLK), .en(1'b1), .Q(AC));
endmodule
